# Fritzing sketch FlickerNoise (saved by Fritzing 0.9.2b)
breadboards: 1

parts:
  パーツ1 = Arduino Uno (Rev3)
  R1 = Resistor [tolerance=±5% resistance=510 package=THT]
  R2 = Resistor [tolerance=±5% resistance=510 package=THT]
  R3 = Resistor [tolerance=±5% resistance=510 package=THT]
  LED1 = LED - 5mm [color="Red (633nm)" package="5 mm [THT]"]
  LED2 = LED - 5mm [color="Red (633nm)" package="5 mm [THT]"]
  LED3 = LED - 5mm [color="Red (633nm)" package="5 mm [THT]"]

nets:
  N1: パーツ1.D9_PWM, R3.Pin_1
  N2: パーツ1.D10_PWM/SS, R2.Pin_1
  N3: パーツ1.D11_PWM/MOSI, R1.Pin_1
  N4: パーツ1.GND, LED1.cathode, LED2.cathode, LED3.cathode
  N5: R1.Pin_0, LED1.anode
  N6: R2.Pin_0, LED2.anode
  N7: R3.Pin_0, LED3.anode

// code stored in the sketch: FlickerNoise.ino
const int LED_NUM = 3;				//Number of LED
const int LED[] = {9,10,11};	//Set LED pin number
const int TIME = 100;

float curValue[LED_NUM];			//Current value for each LED (0 ~ 1.0)

void setup() {
  Serial.begin(9600);					//for debug
  for(int i = 0; i < LED_NUM; i++){
    pinMode(LED[i], OUTPUT);								//Set each LED pin as OUTPUT
    curValue[i] = random(10, 90) / 100.0;		//Set initial value (1.0 ~ 9.0)
  }
}

void loop() {
	int value;
	for (int i = 0; i < LED_NUM; i++) {
		value = chaos(i);
		analogWrite(LED[i], value);
		//Serial.print("PIN");
		//Serial.print(i);
		//Serial.print(":");
		//Serial.print(value);
		//Serial.print(",");
	}
	Serial.println(value);
	delay(TIME);
}

/*
intermittent chaos method
input:[idx] index of LED pin
output:next value
*/
int chaos(int idx){
  float x = curValue[idx];

  if(x < 0.5){
    x = x + 2 * pow(x, 2);
  } else {
    x = x - 2 * pow((1.0 - x), 2);
  }

	//reset value in case of too lower or higher value
  if(x < 0.05 || x > 0.998){
    x = random(10,90) / 100.0;
  }
  
  curValue[idx] = x;
  x = x * 255;
  return (unsigned int) x;
}
